# Fritzing sketch PCB Design (saved by Fritzing 0.9.3b)
circuit board: 5.42969cm x 4.28574cm
breadboards: 1

parts:
  Part1 = Adafruit AMG8833 8x8 GRID EYE
  Raspberry_Pi_1 = Raspberry Pi 3 [part_number=RPI-3-V1.2]

nets:
  3V3: Part1.VIN, Raspberry_Pi_1.3v3, Raspberry_Pi_1.3V3
  GND: Part1.GND, Raspberry_Pi_1.GND
  N1: Part1.SDA, Raspberry_Pi_1.GPIO2
  N2: Part1.SCL, Raspberry_Pi_1.GPIO3
